// Logisim project hi.circ as structural Verilog
module Warmup (
  input  in_1
);

  wire clock_1_out, d_ff_1_q;

  Clock #(.highDuration(3), .lowDuration(3), .phaseOffset(1)) clock_1 (.out(clock_1_out));
  D_Flip_Flop #(.trigger("high")) d_ff_1 (.D(in_1), .clk(clock_1_out), .Q(d_ff_1_q));  // open: Qn, preset, reset
  LED led_1 (.in(d_ff_1_q));
endmodule

module FA (
  input  B,
  input  A,
  input  Cin,
  output S,
  output Cout
);

  wire and_1_out, and_2_out, xor_1_out;

  xor xor_1 (xor_1_out, A, B);
  and and_1 (and_1_out, A, B);
  xor xor_2 (S, xor_1_out, Cin);
  and and_2 (and_2_out, Cin, xor_1_out);
  or or_1 (Cout, and_1_out, and_2_out);
endmodule

module ADDSUB4 (
  input  Sub,
  input  [3:0] B,
  input  [3:0] A,
  output [3:0] S,
  output C3,
  output C2,
  output C1,
  output Z,
  output N,
  output C,
  output V
);

  wire xor_1_out, xor_2_out, xor_3_out, xor_4_out, xor_5_out, xor_6_out;

  xor xor_1 (xor_1_out, Sub, B[0]);
  xor xor_2 (xor_2_out, Sub, B[1]);
  xor xor_3 (xor_3_out, Sub, B[2]);
  xor xor_4 (xor_4_out, Sub, B[3]);
  FA fa_1 (.B(xor_1_out), .A(A[0]), .Cin(Sub), .S(S[0]), .Cout(C1));
  FA fa_2 (.B(xor_2_out), .A(A[1]), .Cin(C1), .S(S[1]), .Cout(C2));
  FA fa_3 (.B(xor_3_out), .A(A[2]), .Cin(C2), .S(S[2]), .Cout(C3));
  xor xor_5 (xor_5_out, N, xor_4_out);
  and and_1 (V, xor_5_out, xor_6_out);
  xor xor_6 (xor_6_out, N, A[3]);
  FA fa_4 (.B(xor_4_out), .A(A[3]), .Cin(C3), .S(N), .Cout(C));
  nor nor_1 (Z, S[0], S[1], S[2], N);

  assign S[3] = N;
endmodule

module ALU8 (
  input  [7:0] A,
  input  [2:0] OP,
  input  [7:0] B,
  input  [7:0] in_4,
  input  [7:0] in_5,
  output [7:0] R,
  output Z,
  output LT
);

  wire [7:0] adder_1_out, adder_2_out, and_1_out, multiplexer_1_out, multiplexer_2_out, not_1_out, or_1_out,
       subtractor_1_out, subtractor_2_out, xor_1_out;

  assign not_1_out = ~A;  // NOT_Gate not_1, 8 bits wide
  Adder adder_1 (.a(A), .b(B), .out(adder_1_out));  // open: cin, cout
  Adder adder_2 (.a(A), .b(in_4), .out(adder_2_out));  // open: cin, cout
  Subtractor subtractor_1 (.a(A), .b(B), .out(subtractor_1_out));  // open: bin, bout
  Subtractor subtractor_2 (.a(A), .b(in_5), .out(subtractor_2_out));  // open: bin, bout
  assign and_1_out = A & B;  // AND_Gate and_1, 8 bits wide
  assign or_1_out = A | B;  // OR_Gate or_1, 8 bits wide
  assign xor_1_out = A ^ B;  // XOR_Gate xor_1, 8 bits wide
  Multiplexer #(.select(2), .width(8)) multiplexer_1 (
    .in0(adder_1_out), .in1(adder_2_out), .in2(subtractor_1_out), .in3(subtractor_2_out),
    .out(multiplexer_1_out), .sel(OP[1:0]));
  Multiplexer #(.select(2), .width(8)) multiplexer_2 (
    .in0(and_1_out), .in1(or_1_out), .in2(not_1_out), .in3(xor_1_out), .out(multiplexer_2_out), .sel(OP[1:0]));
  Multiplexer #(.width(8)) multiplexer_3 (.in0(multiplexer_1_out), .in1(multiplexer_2_out), .out(R), .sel(OP[2]));
  nor nor_1 (Z, R[7], R[6], R[5], R[4], R[3], R[2], R[1], R[0]);
  con con_1 (.A7(A[7]), .B7(B[7]), .R7(R[7]), .LT(LT));
endmodule

module con (
  input  A7,
  input  B7,
  input  R7,
  output LT
);

  wire and_1_out, and_2_out, not_1_out, not_2_out, xor_1_out;

  not not_1 (not_1_out, B7);
  xor xor_1 (xor_1_out, A7, B7);
  and and_1 (and_1_out, A7, not_1_out);
  not not_2 (not_2_out, xor_1_out);
  and and_2 (and_2_out, not_2_out, R7);
  or or_1 (LT, and_1_out, and_2_out);
endmodule

module DLATCH (
  input  E,
  input  D,
  output Q
);

  Multiplexer multiplexer_1 (.in0(Q), .in1(D), .out(Q), .sel(E));
endmodule

module TN3 (
  input  in_1,
  input  D,
  input  in_3,
  input  in_4,
  output Q1,
  output Q2,
  output out_7,
  output out_8
);

  wire d_ff_2_q, dlatch_2_q;

  D_Flip_Flop d_ff_1 (.D(D), .clk(in_1), .Q(Q2), .preset(in_3), .reset(in_4));  // open: Qn
  D_Flip_Flop d_ff_2 (.D(D), .clk(in_1), .Q(d_ff_2_q));  // open: Qn, preset, reset
  D_Flip_Flop d_ff_3 (.D(d_ff_2_q), .clk(in_1), .Q(out_8));  // open: Qn, preset, reset
  DLATCH dlatch_1 (.E(in_1), .D(D), .Q(Q1));
  DLATCH dlatch_2 (.E(in_1), .D(D), .Q(dlatch_2_q));
  DLATCH dlatch_3 (.E(in_1), .D(dlatch_2_q), .Q(out_7));
endmodule

module DFF_MS (
  input  D,
  input  CLK,
  output Q
);

  wire dlatch_1_q, not_1_out;

  not not_1 (not_1_out, CLK);
  DLATCH dlatch_1 (.E(not_1_out), .D(D), .Q(dlatch_1_q));
  DLATCH dlatch_2 (.E(CLK), .D(dlatch_1_q), .Q(Q));
endmodule

module REGFILE (
  input  [1:0] RA,
  input  [7:0] DIN,
  input  [1:0] RD,
  input  WE,
  input  CLK,
  input  [1:0] RB,
  output [7:0] R0,
  output [7:0] R1,
  output [7:0] QA,
  output [7:0] R2,
  output [7:0] QB,
  output [7:0] R3
);

  wire decoder_1_out0, decoder_1_out1, decoder_1_out2, decoder_1_out3;

  Decoder #(.select(2)) decoder_1 (
    .out0(decoder_1_out0), .out1(decoder_1_out1), .out2(decoder_1_out2), .out3(decoder_1_out3), .sel(RD),
    .en(WE));
  Register register_1 (.D(DIN), .en(CLK), .clk(decoder_1_out0), .Q(R0));  // open: clr
  Register register_2 (.D(DIN), .en(CLK), .clk(decoder_1_out1), .Q(R1));  // open: clr
  Register register_3 (.D(DIN), .en(CLK), .clk(decoder_1_out2), .Q(R2));  // open: clr
  Register register_4 (.D(DIN), .en(CLK), .clk(decoder_1_out3), .Q(R3));  // open: clr
  Multiplexer #(.select(2), .width(8)) multiplexer_1 (.in0(R0), .in1(R1), .in2(R2), .in3(R3), .out(QA), .sel(RA));
  Multiplexer #(.select(2), .width(8)) multiplexer_2 (.in0(R0), .in1(R1), .in2(R2), .in3(R3), .out(QB), .sel(RB));
endmodule

module DATAPATH (
  input  [2:0] OP,
  input  [1:0] RA,
  input  [7:0] IMM,
  input  [1:0] RD,
  input  SRC,
  input  WE,
  input  CLK,
  input  [1:0] RB,
  output R0,
  output R1,
  output R2,
  output R3,
  output R,
  output Z
);

  wire [1:1] undriven;
  wire [7:0] alu8_1_r, regfile_1_qa, regfile_1_qb;

  REGFILE regfile_1 (
    .RA(RA), .RD(RD), .WE(WE), .CLK(CLK), .RB(RB), .QA(regfile_1_qa), .QB(regfile_1_qb));  // open: DIN, R0, R1, R2, R3
  ALU8 alu8_1 (.A(regfile_1_qa), .OP(OP), .B(regfile_1_qb), .R(alu8_1_r));  // open: in_4, in_5, Z, LT
  Multiplexer #(.select(2), .width(8)) multiplexer_1 (
    .in0(alu8_1_r), .in1(IMM), .sel({undriven[1], SRC}));  // open: in2, in3, out
  // Pins of 1 and 2 bits meet at {undriven[1], SRC}
endmodule
